# Fritzing sketch sketch (saved by Fritzing 0.9.2b)

parts:
  Squix1 = OLED 0.96" 128x64 I2C SSD1306
  U1 = NodeMCU V1.0

nets:
  VCC: Squix1.VCC, U1.3V3
  GND: Squix1.GND, U1.GND
  N1: Squix1.SCL, U1.D1
  N2: Squix1.SCA, U1.D2

custom parts:
  NodeMCU V1.0: ESP8266 based NodeMCU
